# Fritzing sketch sketch1 (saved by Fritzing 0.9.3b)
breadboards: 1

parts:
  Part1 = Arduino Mega 2560 (Rev3)
  LCD1 = LCD screen
  R1 = Trimmer Potentiometer [maximum_resistance=10kΩ package=THT]
  R2 = Resistor [tolerance=±5% resistance=220 package=THT]
  KEYPAD1 = Membrane Matrix Keypad

nets:
  GND: Part1.GND, LCD1.VSS, LCD1.R/W, LCD1.LED-, R1.leg2
  5V: Part1.5V, LCD1.VDD, R1.leg1, R2.Pin_1
  N1: Part1.D22, KEYPAD1.7
  N2: Part1.D23, LCD1.DB7
  N3: Part1.D24, KEYPAD1.6
  N4: Part1.D25, LCD1.DB6
  N5: Part1.D26, KEYPAD1.5
  N6: Part1.D27, LCD1.DB5
  N7: Part1.D28, KEYPAD1.4
  N8: Part1.D29, LCD1.DB4
  N9: Part1.D30, KEYPAD1.3
  N10: Part1.D31, LCD1.E
  N11: Part1.D32, KEYPAD1.2
  N12: Part1.D33, LCD1.RS
  N13: Part1.D34, KEYPAD1.1
  N14: LCD1.V0, R1.wiper
  N15: LCD1.LED+, R2.Pin_0

custom parts:
  Membrane Matrix Keypad: Membrane Matrix 3x4 Keypad
